// Logisim project T1.circ as structural Verilog
module H (
  input  A,
  input  B,
  input  C,
  input  D,
  output F1
);

  wire and_1_out, and_2_out, and_3_out, not_1_out, not_2_out, not_3_out;

  not not_1 (not_1_out, A);
  and and_1 (and_1_out, not_1_out, not_2_out);
  not not_2 (not_2_out, C);
  not not_3 (not_3_out, A);
  and and_2 (and_2_out, not_3_out, D);
  and and_3 (and_3_out, A, B);
  or or_1 (F1, and_1_out, and_2_out, and_3_out);
endmodule

module a (
  input  A,
  input  B,
  input  C,
  input  D,
  output F1
);

  wire and_1_out, and_2_out, and_3_out, not_1_out, not_2_out;

  not not_1 (not_1_out, A);
  and and_1 (and_1_out, not_1_out, D);
  and and_2 (and_2_out, B, not_2_out);
  not not_2 (not_2_out, C);
  and and_3 (and_3_out, A, B);
  or or_1 (F1, and_1_out, and_2_out, and_3_out);
endmodule

module p (
  input  A,
  input  B,
  input  C,
  input  D,
  output F1
);

  wire and_1_out, and_2_out, and_3_out, not_1_out, not_2_out, not_3_out, not_4_out;

  not not_1 (not_1_out, A);
  and and_1 (and_1_out, not_1_out, not_2_out);
  not not_2 (not_2_out, B);
  not not_3 (not_3_out, B);
  and and_2 (and_2_out, not_3_out, C);
  and and_3 (and_3_out, A, not_4_out);
  not not_4 (not_4_out, D);
  or or_1 (F1, and_1_out, and_2_out, and_3_out);
endmodule
